# Fritzing sketch Mini Fonte Regulável Versão 0.0.1 (saved by Fritzing 0.9.3b)
circuit board: 6.64078cm x 2.8654cm
breadboards: 1

parts:
  R1 = Resistor [tolerance=±5% resistance=240 package=THT]
  U1 = Voltage Regulator [package=to220-adj]
  C2 = Electrolytic Capacitor [capacitance=10µF voltage=50V package="300 mil [THT, electrolytic]"]
  J1 = female pin header, 2 pins [form="♀ (female)"]
  J2 = male pin header, 2 pins [form="♂ (male)"]
  C1 = Ceramic Capacitor [capacitance=100nF package="200 mil [THT, multilayer]"]
  R2 = Rotary Potentiometer (Large) [maximum_resistance=5kΩ package=THT]

nets:
  N1: R1.Pin_0, U1.ADJ, R2.leg1, R2.wiper
  N2: R1.Pin_1, U1.OUT, C2.+, J2.pin1
  N3: U1.IN, J1.pin1, C1.1
  GND: C2.-, J1.pin2, J2.pin2, C1.0, R2.leg2

notes:
  Vout = 1.25V (1+ R1/R2))+ (Iadj * R1)
